# Fritzing sketch led_clock (saved by Fritzing 0.9.10b)
breadboards: 1

parts:
  Part1 = Arduino Nano (Rev3.0) (ICSP)
  S2 = Round Pushbutton
  S3 = Round Pushbutton
  PCB2 = RTC_DS1302_module
  Part2 = Adafruit TSL2561 [part_number="Adafruit #439"]
  R1 = Resistor [tolerance=±5% power=0.25 resistance=3.3k package=THT]
  R2 = Resistor [tolerance=±5% power=0.25 resistance=3.3k package=THT]
  RGB_SMD_LED1 = SMD RGB LED (WS2812) [package=5050]
  RGB_SMD_LED2 = SMD RGB LED (WS2812) [package=5050]

nets:
  GND: Part1.GND, S2.leg0, S3.leg1, PCB2.GND, Part2.GND, RGB_SMD_LED1.VSS, RGB_SMD_LED2.VSS
  N1: Part1.D2, RGB_SMD_LED1.DIn
  N2: Part1.D3, RGB_SMD_LED2.DIn
  N3: Part1.D5, PCB2.RST
  N4: Part1.D6, PCB2.DAT
  N5: Part1.D7, PCB2.CLK
  N6: Part1.D8, S3.leg0
  N7: Part1.D9, S2.leg1
  VCC: Part1.5V, PCB2.VCC, RGB_SMD_LED1.VCC, RGB_SMD_LED2.VCC
  N8: Part1.A5, Part2.SCL, R1.Pin_0
  N9: Part1.A4, Part2.SDA, R2.Pin_0
  3V3: Part1.3V3, Part2.VIN
  N10: R1.Pin_1, R2.Pin_1

custom parts:
  RTC_DS1302_module: Arduino module DS1302 SPI Real Time Clock
  Adafruit TSL2561: The TSL2561 luminosity sensor is an advanced digital light sensor, ideal for use in a wide range of light situations. Compared to low cost CdS cells, this sensor is more precise, allowing for exact lux calculations and can be configured for different gain/timing ranges to detect light ranges from up to 0.1 - 40,000+ Lux on the fly. The best part of this sensor is that it contains both infrared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
